// Logisim project mct4.circ as structural Verilog: 2 circuits, main circuit main
module main (
  input  in_1,
  input  in_2,
  input  in_3,
  input  in_4,
  input  in_5,
  input  in_6,
  input  in_7,
  input  in_8,
  input  in_9,
  input  in_10,
  input  in_11,
  input  in_12,
  input  in_13,
  input  in_14
);

  wire and_1_out, apu_1_carry, Clock_out, comparator_1_eq, Reset_out;
  wire [3:0] controlled_buffer_1_out, MAR_q, PC_q;
  wire [7:0] A_q, apu_1_sum, B_q, IR_q, ram_1_dout, undriven;
  wire [7:4] controlled_buffer_1_out_2;

  RAM #(.addrWidth(4), .enables("line")) ram_1 (
    .addr(MAR_q), .we(in_5), .clk(Clock_out), .din({controlled_buffer_1_out_2, controlled_buffer_1_out}),
    .dout(ram_1_dout));
  Register #(.width(4)) MAR (.D(controlled_buffer_1_out), .en(in_2), .clk(Clock_out), .Q(MAR_q), .clr(Reset_out));
  Register IR (
    .D({controlled_buffer_1_out_2, controlled_buffer_1_out}), .en(in_14), .clk(Clock_out), .Q(IR_q),
    .clr(Reset_out));
  assign {controlled_buffer_1_out_2, controlled_buffer_1_out} = in_6 ? ram_1_dout : 8'bz;  // Controlled_Buffer controlled_buffer_1
  assign {controlled_buffer_1_out_2, controlled_buffer_1_out} = in_12 ? {4'b0000, IR_q[3:0]} : 8'bz;  // Controlled_Buffer controlled_buffer_2
  Button Reset (.out(Reset_out));
  Button Clock (.out(Clock_out));
  LedBar ledbar_1 (
    .led0(controlled_buffer_1_out_2[7]), .led1(controlled_buffer_1_out_2[6]),
    .led2(controlled_buffer_1_out_2[5]), .led3(controlled_buffer_1_out_2[4]),
    .led4(controlled_buffer_1_out[3]), .led5(controlled_buffer_1_out[2]), .led6(controlled_buffer_1_out[1]),
    .led7(controlled_buffer_1_out[0]));
  // DipSwitch dipswitch_1: pin names not known
  assign {controlled_buffer_1_out_2, controlled_buffer_1_out} = in_1 ? undriven : 8'bz;  // Controlled_Buffer controlled_buffer_3
  Register A (
    .D({controlled_buffer_1_out_2, controlled_buffer_1_out}), .en(in_4), .clk(Clock_out), .Q(A_q),
    .clr(Reset_out));
  Register B (
    .D({controlled_buffer_1_out_2, controlled_buffer_1_out}), .en(in_8), .clk(Clock_out), .Q(B_q),
    .clr(Reset_out));
  assign {controlled_buffer_1_out_2, controlled_buffer_1_out} = in_13 ? {4'b0000, PC_q} : 8'bz;  // Controlled_Buffer controlled_buffer_4
  assign {controlled_buffer_1_out_2, controlled_buffer_1_out} = in_3 ? A_q : 8'bz;  // Controlled_Buffer controlled_buffer_5
  assign {controlled_buffer_1_out_2, controlled_buffer_1_out} = in_9 ? apu_1_sum : 8'bz;  // Controlled_Buffer controlled_buffer_6
  Counter #(.max('hf), .width(4)) PC (
    .clr(Reset_out), .load(in_10), .up(1'b1), .count(in_11), .clk(Clock_out), .D(controlled_buffer_1_out),
    .Q(PC_q));  // open: carry
  apu apu_1 (.A(A_q), .B(B_q), .AS(in_7), .sum(apu_1_sum), .carry(apu_1_carry));
  D_Flip_Flop Carry (.D(apu_1_carry), .clk(and_1_out), .reset(Reset_out));  // open: Q, Qn, preset
  D_Flip_Flop Zero (.D(comparator_1_eq), .clk(and_1_out), .reset(Reset_out));  // open: Q, Qn, preset
  Comparator comparator_1 (.a(apu_1_sum), .b({8{1'b0}}), .eq(comparator_1_eq));  // open: gt, lt
  and and_1 (and_1_out, Clock_out, in_9);
endmodule

module apu (
  input  [7:0] A,
  input  [7:0] B,
  input  AS,
  output [7:0] sum,
  output carry
);

  wire adder_1_cout, subtractor_1_bout;
  wire [7:0] adder_1_out, subtractor_1_out;

  Adder adder_1 (.a(A), .b(B), .out(adder_1_out), .cout(adder_1_cout));  // open: cin
  Subtractor subtractor_1 (.a(A), .b(B), .out(subtractor_1_out), .bout(subtractor_1_bout));  // open: bin
  Multiplexer #(.width(8)) multiplexer_1 (.in0(adder_1_out), .in1(subtractor_1_out), .out(sum), .sel(AS));
  Multiplexer multiplexer_2 (.in0(adder_1_cout), .in1(subtractor_1_bout), .out(carry), .sel(AS));
endmodule
